# Fritzing sketch pc-audio-mixer (saved by Fritzing 1.0.6)
breadboards: 2

parts:
  ADC1 = MCP3008 [package=dil16]
  Mod1 = Raspberry Pi Pico
  C1 = Capacitor [mn=100nF package=cap-pth-small2]
  C2 = Capacitor [mn=100nF package=cap-pth-small2]
  C3 = Electrolytic Capacitor [capacitance=1µF voltage=35V package="100 mil [THT, electrolytic]"]
  R1 = Rotary Potentiometer (Large) [maximum_resistance=100kΩ knob_status=50% power=0.5W package=THT]
  R2 = Resistor [tolerance=±5% power=0.25W resistance=220 package=THT]
  C4 = Capacitor [package=cap-pth-small2]
  R3 = Rotary Potentiometer (Large) [maximum_resistance=100kΩ knob_status=50% power=0.5W package=THT]
  R4 = Rotary Potentiometer (Large) [maximum_resistance=100kΩ knob_status=50% power=0.5W package=THT]
  R5 = Rotary Potentiometer (Large) [maximum_resistance=100kΩ knob_status=50% power=0.5W package=THT]
  R6 = Resistor [tolerance=±5% power=0.25W resistance=220 package=THT]
  R7 = Resistor [tolerance=±5% power=0.25W resistance=220 package=THT]
  R8 = Resistor [tolerance=±5% power=0.25W resistance=220 package=THT]
  C5 = Capacitor [package=cap-pth-small2]
  C6 = Capacitor [package=cap-pth-small2]
  C7 = Capacitor [package=cap-pth-small2]
  C8 = Capacitor [package=cap-pth-small2]
  R9 = Rotary Potentiometer (Large) [maximum_resistance=100kΩ knob_status=50% power=0.5W package=THT]
  R10 = Resistor [tolerance=±5% power=0.25W resistance=220 package=THT]
  C9 = Capacitor [package=cap-pth-small2]
  R11 = Rotary Potentiometer (Large) [maximum_resistance=100kΩ knob_status=50% power=0.5W package=THT]
  R12 = Resistor [tolerance=±5% power=0.25W resistance=220 package=THT]
  C10 = Capacitor [package=cap-pth-small2]
  R13 = Rotary Potentiometer (Large) [maximum_resistance=100kΩ knob_status=50% power=0.5W package=THT]
  R14 = Resistor [tolerance=±5% power=0.25W resistance=220 package=THT]
  C11 = Capacitor [package=cap-pth-small2]
  R15 = Rotary Potentiometer (Large) [maximum_resistance=100kΩ knob_status=50% power=0.5W package=THT]
  R16 = Resistor [tolerance=±5% power=0.25W resistance=220 package=THT]

nets:
  N1: ADC1.CH0, R2.Pin_0, C4.2
  N2: ADC1.CH1, R6.Pin_0, C5.2
  N3: ADC1.CH2, R7.Pin_0, C6.2
  N4: ADC1.CH3, R8.Pin_0, C7.2
  N5: ADC1.CH4, C8.2, R10.Pin_0
  N6: ADC1.CH5, C9.2, R12.Pin_0
  N7: ADC1.CH6, C10.2, R14.Pin_0
  N8: ADC1.CH7, C11.2, R16.Pin_0
  N9: ADC1.DGND, ADC1.AGND, Mod1.pin_3, Mod1.pin_8, Mod1.pin_13, Mod1.pin_18, Mod1.pin_23, Mod1.pin_28, Mod1.pin_33, Mod1.pin_38, C1.1, C2.1, C3.-, R1.leg2, C4.1, R3.leg2, R4.leg2, R5.leg2, C5.1, C6.1, C7.1, C8.1, R9.leg2, C9.1, R11.leg2, C10.1, C11.1, R15.leg2
  N10: ADC1.CS/SHDN, Mod1.pin_22
  N11: ADC1.Din, Mod1.pin_25
  N12: ADC1.Dout, Mod1.pin_21
  N13: ADC1.CLK, Mod1.pin_24
  N14: ADC1.VREF, ADC1.VDD, Mod1.pin_36, C1.2, C2.2, C3.+, R1.leg1, R3.leg1, R4.leg1, R5.leg1, R9.leg1, R11.leg1, R13.leg1, R15.leg1
  N15: R1.wiper, R2.Pin_1
  N16: R3.wiper, R6.Pin_1
  N17: R4.wiper, R7.Pin_1
  N18: R5.wiper, R8.Pin_1
  N19: R9.wiper, R10.Pin_1
  N20: R11.wiper, R12.Pin_1
  N21: R13.wiper, R14.Pin_1
  N22: R15.wiper, R16.Pin_1

custom parts:
  Raspberry Pi Pico: Raspberry Pi Pico. Based around the RP2040 microcontroller the Pico is a low cost microcontroller device bringing Raspberry Pi quality, cost, and easy of use to the microcontroller space. Jan 2021, Split part in to two versions: tht (this one) and SMD. This one will drill holes for a .1 in header in pcb to allow plugging in the module as well as providing pads to solder the module to the top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
